# Fritzing sketch Circuit layout for text entry (saved by Fritzing 0.9.3b)
breadboards: 1

parts:
  S1 = Pushbutton [package="[THT]"]
  S2 = Pushbutton [package="[THT]"]
  S3 = Pushbutton [package="[THT]"]
  S4 = Pushbutton [package="[THT]"]
  S6 = Pushbutton [package="[THT]"]
  S7 = Pushbutton [package="[THT]"]
  S8 = Pushbutton [package="[THT]"]
  Part1 = RedBear-Duo

nets:
  N1: S1.Pin_1, S1.Pin_2, Part1.D6
  N2: S1.Pin_3, S1.Pin_4, S2.Pin_3, S2.Pin_4, S3.Pin_3, S3.Pin_4, S4.Pin_3, S4.Pin_4, S6.Pin_3, S6.Pin_4, S7.Pin_3, S7.Pin_4, S8.Pin_3, S8.Pin_4, Part1.GND
  N3: S2.Pin_1, S2.Pin_2, Part1.D5
  N4: S3.Pin_1, S3.Pin_2, Part1.D2, Part1.D4
  N5: S4.Pin_1, S4.Pin_2, Part1.D3
  N6: S6.Pin_1, S6.Pin_2, Part1.D0
  N7: S7.Pin_1, S7.Pin_2, Part1.D1
  N8: S8.Pin_1, S8.Pin_2

custom parts:
  RedBear-Duo: Duo is a thumb-size development board made to simplify the building process of Internet of Things (IoT). This part is a modification of the Particle Photon part by Brett Walach,Fabian Althaus
